# Fritzing sketch Arduino (UNO) Rc Car (Fritzing Diagram) (saved by Fritzing 1.0.4)

parts:
  L298N1 = L298N DC motor driver
  M1 = gear-motor  # not connected
  9-12V_Battery = 4 x AAA Battery Mount [internal_resistance=0.1Ω]
  M3 = gear-motor  # not connected
  M4 = gear-motor  # not connected
  Part3 = Bluetooth HC-05 Macho  # not connected
  U1 = SWITCH-SPST-2 [package=switch-spst-vertical]
  M2 = gear-motor  # not connected
  Part1 = Arduino Uno (Rev3) - ICSP

nets:
  N1: L298N1.12V, U1.O
  N2: L298N1.GND, 9-12V_Battery.-
  N3: L298N1.5V#9, L298N1.ENA
  N4: L298N1.5V#10, L298N1.ENB
  N5: L298N1.IN1, Part1.ICSP_MISO, Part1.D12/MISO
  N6: L298N1.IN2, Part1.D11_PWM/MOSI
  N7: L298N1.IN3, Part1.D10_PWM/SS
  N8: L298N1.IN4, Part1.D9_PWM
  N9: 9-12V_Battery.+, U1.P

notes:
  Do not forget to connect the small contactors of the L298N to activate PWM

custom parts:
  L298N DC motor driver: 2x DC motor driver with 78M05 positive voltage regulator (7..35 V) L298N: max 46 V, 2 A Set 5 V Enable jumper to enable 5 V regultor (needed for the L298N) and +5 V output at screw terminal or supply external +5 V at screw terminal Set ENA and/or ENB to +5 V to enable motor permanently or supply ENA and/or ENB with PWM signal IN1 and IN2 set rotation directory for motor A (OUT1/OUT2) IN2 and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
